// Logisim project S2-T17.circ as structural Verilog
module _7_segment_driver (
  input  A,
  input  B,
  input  C,
  input  D,
  output a_2,
  output b_2,
  output c_2,
  output d_2,
  output e,
  output f,
  output g
);

  wire and_1_out, and_2_out, and_3_out, and_4_out, and_5_out, and_6_out, not_1_out, not_2_out, not_3_out,
       not_4_out, not_5_out, not_6_out, xor_1_out, xor_2_out, xor_3_out, xor_4_out, xor_5_out;

  not not_1 (not_1_out, C);
  not not_2 (not_2_out, A);
  not not_3 (not_3_out, B);
  not not_4 (not_4_out, D);
  and and_1 (and_1_out, C, not_4_out);
  and and_2 (and_2_out, not_1_out, B);
  and and_3 (and_3_out, not_4_out, not_1_out);
  and and_4 (and_4_out, not_4_out, B);
  and and_5 (and_5_out, not_3_out, not_4_out);
  or or_1 (f, A, and_2_out, and_3_out, and_4_out);
  xor xor_1 (xor_1_out, A, C);
  xor xor_2 (xor_2_out, B, C);
  xor xor_3 (xor_3_out, B, D);
  xor xor_4 (xor_4_out, B, not_6_out);
  xor xor_5 (xor_5_out, C, D);
  or or_2 (g, A, xor_2_out, and_4_out);
  not not_5 (not_5_out, xor_3_out);
  and and_6 (and_6_out, not_2_out, C, not_3_out, not_4_out);
  or or_3 (b_2, not_3_out, not_6_out);
  not not_6 (not_6_out, xor_5_out);
  or or_4 (e, and_5_out, and_1_out);
  or or_5 (a_2, xor_1_out, not_5_out);
  not not_7 (c_2, and_6_out);
  or or_6 (d_2, and_1_out, A, xor_4_out);

  // Notes on the sheet:
  //   SEVEN SEGMENT DISPLAY DRIVER
  //   f
  //   e
  //   a
  //   ---------
  //   |
  //   |
  //   b
  //   |
  //   |
  //   --------
  //   |
  //   |
  //   g
  //   c
  //   |
  //   |
  //   --------
  //   d
endmodule

module register (
  input  a3,
  input  a2,
  input  a1,
  input  a0,
  input  clear,
  input  enable_by_clock,
  output o3,
  output o2,
  output o1,
  output o0
);

  wire undriven;

  Register_part #(.width(1)) register_1 (.D(a3), .en(undriven), .Q(o3), .clk(enable_by_clock), .clr(clear));
  Register_part #(.width(1)) register_2 (.D(a2), .Q(o2), .clk(enable_by_clock), .clr(clear));  // open: en
  Register_part #(.width(1)) register_3 (.D(a1), .Q(o1), .clk(enable_by_clock), .clr(clear));  // open: en
  Register_part #(.width(1)) register_4 (.D(a0), .Q(o0), .clk(enable_by_clock), .clr(clear));  // open: en
endmodule

module counter (
  output FASTEST,
  output MEDIUM,
  output SLOWEST
);

  wire clock_1_out;

  Clock clock_1 (.out(clock_1_out));
  J_K_Flip_Flop j_k_ff_1 (.J(1'b1), .clk(clock_1_out), .K(1'b1), .Q(FASTEST));  // open: Qn, preset, en, reset
  J_K_Flip_Flop j_k_ff_2 (.J(1'b1), .clk(FASTEST), .K(1'b1), .Q(MEDIUM));  // open: Qn, preset, en, reset
  J_K_Flip_Flop j_k_ff_3 (.J(1'b1), .clk(MEDIUM), .K(1'b1), .Q(SLOWEST));  // open: Qn, preset, en, reset

  // Notes on the sheet:
  //   Counter for use in PRBS FLUX
endmodule

// mux
module select_player_score_bits (
  input  s1,
  input  s0,
  input  a0p1,
  input  a1p1,
  input  a2p1,
  input  a3p1,
  input  a4p1,
  input  a5p1,
  input  a0p2,
  input  a1p2,
  input  a2p2,
  input  a3p2,
  input  a4p2,
  input  a5p2,
  input  a0p3,
  input  a1p3,
  input  a2p3,
  input  a3p3,
  input  a4p3,
  input  a5p3,
  output a0,
  output a1,
  output a2,
  output a3,
  output a4,
  output a5
);

  wire and_1_out, multiplexer_1_out, multiplexer_2_out, multiplexer_3_out, multiplexer_4_out,
       multiplexer_5_out, multiplexer_6_out;

  Multiplexer multiplexer_1 (.in0(a0p1), .in1(a0p2), .out(multiplexer_1_out), .sel(s1), .en(1'b1));
  Multiplexer multiplexer_2 (.in0(a1p1), .in1(a1p2), .out(multiplexer_2_out), .sel(s1), .en(1'b1));
  Multiplexer multiplexer_3 (.in0(a2p1), .in1(a2p2), .out(multiplexer_3_out), .sel(s1), .en(1'b1));
  Multiplexer multiplexer_4 (.in0(a3p1), .in1(a3p2), .out(multiplexer_4_out), .sel(s1), .en(1'b1));
  Multiplexer multiplexer_5 (.in0(a4p1), .in1(a4p2), .out(multiplexer_5_out), .sel(s1), .en(1'b1));
  Multiplexer multiplexer_6 (.in0(a5p1), .in1(a5p2), .out(multiplexer_6_out), .sel(s1), .en(1'b1));
  and and_1 (and_1_out, s0, s1);
  Multiplexer multiplexer_7 (.in0(multiplexer_1_out), .in1(a0p3), .out(a0), .sel(and_1_out), .en(1'b1));
  Multiplexer multiplexer_8 (.in0(multiplexer_2_out), .in1(a1p3), .out(a1), .sel(and_1_out), .en(1'b1));
  Multiplexer multiplexer_9 (.in0(multiplexer_3_out), .in1(a2p3), .out(a2), .sel(and_1_out), .en(1'b1));
  Multiplexer multiplexer_10 (.in0(multiplexer_4_out), .in1(a3p3), .out(a3), .sel(and_1_out), .en(1'b1));
  Multiplexer multiplexer_11 (.in0(multiplexer_5_out), .in1(a4p3), .out(a4), .sel(and_1_out), .en(1'b1));
  Multiplexer multiplexer_12 (.in0(multiplexer_6_out), .in1(a5p3), .out(a5), .sel(and_1_out), .en(1'b1));

  // Notes on the sheet:
  //   player code
  //   lsb
  //   msb
  //   Selected Player's bits
endmodule

// demux
module demux_6bit_for_player_scores (
  input  s0,
  input  s1,
  input  a0,
  input  a1,
  input  a2,
  input  a3,
  input  a4,
  input  a5,
  output a0p1,
  output a1p1,
  output a2p1,
  output a3p1,
  output a4p1,
  output a5p1,
  output a0p2,
  output a1p2,
  output a3p2,
  output a4p2,
  output a5p2,
  output a6p2,
  output a0p3,
  output a1p3,
  output a2p3,
  output a3p3,
  output a4p3,
  output a5p3
);

  wire and_1_out, demultiplexer_1_out1, demultiplexer_2_out1, demultiplexer_3_out1, demultiplexer_4_out1,
       demultiplexer_5_out1, demultiplexer_6_out1;

  Demultiplexer demultiplexer_1 (.out0(a0p1), .out1(demultiplexer_1_out1), .in(a0), .sel(s1), .en(1'b1));
  Demultiplexer demultiplexer_2 (.out0(a1p1), .out1(demultiplexer_2_out1), .in(a1), .sel(s1), .en(1'b1));
  Demultiplexer demultiplexer_3 (.out0(a2p1), .out1(demultiplexer_3_out1), .in(a2), .sel(s1), .en(1'b1));
  Demultiplexer demultiplexer_4 (.out0(a3p1), .out1(demultiplexer_4_out1), .in(a3), .sel(s1), .en(1'b1));
  Demultiplexer demultiplexer_5 (.out0(a4p1), .out1(demultiplexer_5_out1), .in(a4), .sel(s1), .en(1'b1));
  Demultiplexer demultiplexer_6 (.out0(a5p1), .out1(demultiplexer_6_out1), .in(a5), .sel(s1), .en(1'b1));
  and and_1 (and_1_out, s0, s1);
  Demultiplexer demultiplexer_7 (.out0(a0p2), .out1(a0p3), .in(demultiplexer_1_out1), .sel(and_1_out), .en(1'b1));
  Demultiplexer demultiplexer_8 (.out0(a1p2), .out1(a1p3), .in(demultiplexer_2_out1), .sel(and_1_out), .en(1'b1));
  Demultiplexer demultiplexer_9 (.out0(a3p2), .out1(a2p3), .in(demultiplexer_3_out1), .sel(and_1_out), .en(1'b1));
  Demultiplexer demultiplexer_10 (.out0(a4p2), .out1(a3p3), .in(demultiplexer_4_out1), .sel(and_1_out), .en(1'b1));
  Demultiplexer demultiplexer_11 (.out0(a5p2), .out1(a4p3), .in(demultiplexer_5_out1), .sel(and_1_out), .en(1'b1));
  Demultiplexer demultiplexer_12 (.out0(a6p2), .out1(a5p3), .in(demultiplexer_6_out1), .sel(and_1_out), .en(1'b1));

  // Notes on the sheet:
  //   player code bits
  //   code lsb
  //   code msb
  //   Player score bits
  //   lsb
  //   msb
  //   player-1 score bits
  //   in register
  //   player-2 score bits 
  //   in register
  //   player-3 score bits 
  //   in register
endmodule

module _5_bit_adder (
  input  b4,
  input  b3,
  input  b2,
  input  b1,
  input  b0,
  input  a4,
  input  a3,
  input  a2,
  input  a1,
  input  a0,
  output o0,
  output o1,
  output o2,
  output o3,
  output o4,
  output o5
);

  wire adder_2_cout, adder_3_cout, adder_4_cout, adder_5_cout;

  Adder #(.width(1)) adder_1 (.a(b4), .b(a4), .out(o4), .cin(adder_2_cout), .cout(o5));
  Adder #(.width(1)) adder_2 (.a(b3), .b(a3), .out(o3), .cin(adder_3_cout), .cout(adder_2_cout));
  Adder #(.width(1)) adder_3 (.a(b2), .b(a2), .out(o2), .cin(adder_4_cout), .cout(adder_3_cout));
  Adder #(.width(1)) adder_4 (.a(b1), .b(a1), .out(o1), .cin(adder_5_cout), .cout(adder_4_cout));
  Adder #(.width(1)) adder_5 (.a(b0), .b(a0), .out(o0), .cin(1'b0), .cout(adder_5_cout));
endmodule

module Register (
  input  a5,
  input  a4,
  input  a3,
  input  a2,
  input  a1,
  input  a0,
  input  clear,
  input  enable_by_clock,
  output o5,
  output o4,
  output o3,
  output o2,
  output o1,
  output o0
);

  Register_part #(.width(1)) register_1 (.D(a5), .Q(o5), .clk(enable_by_clock), .clr(clear));  // open: en
  Register_part #(.width(1)) register_2 (.D(a4), .Q(o4), .clk(enable_by_clock));  // open: en, clr
  Register_part #(.width(1)) register_3 (.D(a3), .Q(o3), .clk(enable_by_clock), .clr(clear));  // open: en
  Register_part #(.width(1)) register_4 (.D(a2), .Q(o2), .clk(enable_by_clock), .clr(clear));  // open: en
  Register_part #(.width(1)) register_5 (.D(a1), .Q(o1), .clk(enable_by_clock), .clr(clear));  // open: en
  Register_part #(.width(1)) register_6 (.D(a0), .Q(o0), .clk(enable_by_clock), .clr(clear));  // open: en
endmodule

module Circle_Points (
  input  L0,
  input  L1,
  input  L2,
  input  L3,
  input  L4,
  output S0,
  output S1,
  output S2
);

  or or_1 (S0, L0, L2, L4);
  or or_2 (S1, L2, L3);
  or or_3 (S2, L0, L1);

  // Notes on the sheet:
  //   Bullseye
  //   2nd inner
  //   middle
  //   penultimate
  //   outer
  //   POINTS ASSIGNMENT TO EACH CONCENTRIC CIRCLE
  //   Points 
  //   point LSB
  //   point bit-1
  //   point MSB
  //   Refer Game description to know exact points assigned
endmodule

module PRBS_FLUX (
  input  L0,
  input  RELEASE,
  input  L2,
  input  READY,
  output L4,
  output L3,
  output L2_2,
  output L1,
  output L0_2
);

  wire _1_q, _2_q, _3_q, _4_q, and_1_out, and_2_out, and_3_out, and_4_out, and_5_out, and_6_out, and_7_out,
       Counter_fastest, Counter_medium, Counter_slowest, multiplexer_1_out, multiplexer_2_out, not_1_out,
       not_2_out, not_3_out, not_4_out, not_5_out, not_6_out, not_7_out, not_8_out, not_9_out, not_10_out,
       not_11_out, not_12_out, not_13_out, xor_1_out;

  not not_1 (not_1_out, L0);
  counter Counter (.FASTEST(Counter_fastest), .MEDIUM(Counter_medium), .SLOWEST(Counter_slowest));
  Multiplexer multiplexer_1 (
    .in0(Counter_slowest), .in1(Counter_medium), .out(multiplexer_1_out), .sel(L2));  // open: en
  Multiplexer multiplexer_2 (
    .in0(multiplexer_1_out), .in1(Counter_fastest), .out(multiplexer_2_out), .sel(not_1_out));  // open: en
  and and_1 (and_1_out, _4_q, _3_q, _2_q, _1_q);
  not not_2 (not_2_out, _2_q);
  and and_2 (and_2_out, not_2_out, _1_q, not_5_out);
  or or_1 (L4, and_1_out, and_2_out);
  and and_3 (and_3_out, multiplexer_2_out, RELEASE);
  not not_3 (not_3_out, _4_q);
  not not_4 (not_4_out, _2_q);
  not not_5 (not_5_out, _3_q);
  and and_4 (and_4_out, not_3_out, _3_q, not_4_out, not_6_out);
  D_Flip_Flop #(.trigger("falling")) _1 (
    .clk(and_3_out), .D(xor_1_out), .Q(_1_q), .preset(READY));  // open: Qn, en, reset
  xor xor_1 (xor_1_out, _3_q, _4_q);
  not not_6 (not_6_out, _1_q);
  not not_7 (not_7_out, _3_q);
  and and_5 (and_5_out, _1_q, _2_q, not_7_out);
  or or_2 (L3, and_4_out, and_5_out);
  D_Flip_Flop #(.trigger("falling")) _2 (.clk(and_3_out), .D(_1_q), .Q(_2_q));  // open: Qn, preset, en, reset
  not not_8 (not_8_out, _2_q);
  not not_9 (not_9_out, _4_q);
  and and_6 (and_6_out, not_9_out, _3_q, not_8_out, _1_q);
  D_Flip_Flop #(.trigger("falling")) _3 (.clk(and_3_out), .D(_2_q), .Q(_3_q));  // open: Qn, preset, en, reset
  not not_10 (not_10_out, _1_q);
  and and_7 (and_7_out, _4_q, _3_q, _2_q, not_10_out);
  or or_3 (L2_2, and_6_out, and_7_out);
  D_Flip_Flop #(.trigger("falling")) _4 (.clk(and_3_out), .D(_3_q), .Q(_4_q));  // open: Qn, preset, en, reset
  not not_11 (not_11_out, _1_q);
  not not_12 (not_12_out, _4_q);
  and and_8 (L1, not_12_out, _2_q, not_11_out);
  not not_13 (not_13_out, _2_q);
  and and_9 (L0_2, _4_q, _3_q, not_13_out);

  // Notes on the sheet:
  //   Darts left in 
  //   The throw count increases with
  //   Quiver 
  //   it the speed of the sequnce change too
  //   Throw Count LSB
  //   Throw Count BIT-2
  //   Qd
  //   Qc
  //   Qb
  //   Qa
  //   PRBS FLUX
  //   A speed varying random sequence generator
  //   OUTER CIRCLE
  //   MSB
  //   PENULTIMATE
  //   4 flip flops used
  //   MIDDLE
  //   2ND INNER 
  //   2^4 -1 sequences
  //   LSB
  //   INNER CIRCLE
  //   RANDOM SEQUENCE GENERATOR
  //   Combinational Logic to light up each concentric circle
  //   using these random sequences generated
endmodule

module _5_bit_bcd_adder (
  input  b4,
  input  b3,
  input  b2,
  input  b1,
  input  b0,
  input  a4,
  input  a3,
  input  a2,
  input  a1,
  input  a0,
  output o0,
  output o1,
  output o2,
  output o3,
  output o4,
  output o5
);

  wire and_1_out, n5_bit_adder_1_o0, n5_bit_adder_1_o1, n5_bit_adder_1_o2, n5_bit_adder_1_o3,
       n5_bit_adder_1_o4, n5_bit_adder_1_o5, n5_bit_adder_2_o5, or_1_out;

  _5_bit_adder u_5_bit_adder_1 (
    .b4(b4), .b3(b3), .b2(b2), .b1(b1), .b0(b0), .a4(a4), .a3(a3), .a2(a2), .a1(a1), .a0(a0),
    .o0(n5_bit_adder_1_o0), .o1(n5_bit_adder_1_o1), .o2(n5_bit_adder_1_o2), .o3(n5_bit_adder_1_o3),
    .o4(n5_bit_adder_1_o4), .o5(n5_bit_adder_1_o5));
  or or_1 (or_1_out, n5_bit_adder_1_o1, n5_bit_adder_1_o2);
  and and_1 (and_1_out, n5_bit_adder_1_o3, or_1_out);
  _5_bit_adder u_5_bit_adder_2 (
    .b4(1'b0), .b3(1'b0), .b2(and_1_out), .b1(and_1_out), .b0(1'b0), .a4(n5_bit_adder_1_o4),
    .a3(n5_bit_adder_1_o3), .a2(n5_bit_adder_1_o2), .a1(n5_bit_adder_1_o1), .a0(n5_bit_adder_1_o0), .o0(o0),
    .o1(o1), .o2(o2), .o3(o3), .o4(o4), .o5(n5_bit_adder_2_o5));
  or or_2 (o5, n5_bit_adder_2_o5, n5_bit_adder_1_o5);
endmodule

module _6_bit_adder (
  input  b4,
  input  b3,
  input  b2,
  input  b1,
  input  b0,
  input  a4,
  input  a3,
  input  a2,
  input  a1,
  input  a0,
  output out_11,
  output o4,
  output o3,
  output o2,
  output o1,
  output o0
);

  wire adder_1_out, adder_3_cout, adder_4_cout, adder_5_cout, adder_6_cout;

  Adder #(.width(1)) adder_1 (.out(adder_1_out), .cout(out_11));  // open: a, b, cin
  Adder #(.width(1)) adder_2 (.a(b4), .b(a4), .out(o4), .cin(adder_3_cout), .cout(adder_1_out));
  Adder #(.width(1)) adder_3 (.a(b3), .b(a3), .out(o3), .cin(adder_4_cout), .cout(adder_3_cout));
  Adder #(.width(1)) adder_4 (.a(b2), .b(a2), .out(o2), .cin(adder_5_cout), .cout(adder_4_cout));
  Adder #(.width(1)) adder_5 (.a(b1), .b(a1), .out(o1), .cin(adder_6_cout), .cout(adder_5_cout));
  Adder #(.width(1)) adder_6 (.a(b0), .b(a0), .out(o0), .cin(1'b0), .cout(adder_6_cout));

  // Notes on the sheet:
  //   PLAYER SCORE ADDER
  //   Given 5 throws, a player can garner
  //   a maximum of 25 points
endmodule

module comparator (
  input  a5,
  input  b5,
  input  a4,
  input  b4,
  input  a3,
  input  b3,
  input  a2,
  input  b2,
  input  a1,
  input  b1,
  input  a0,
  input  b0,
  output less_than,
  output equal
);

  wire and_1_out, and_2_out, and_3_out, and_4_out, and_5_out, and_6_out, comparator_1_eq, comparator_1_gt,
       comparator_2_eq, comparator_2_gt, comparator_3_eq, comparator_3_gt, comparator_4_eq, comparator_4_gt,
       comparator_5_eq, comparator_5_gt, comparator_6_eq, comparator_6_gt, or_1_out;

  Comparator #(.width(1)) comparator_1 (.a(a5), .b(b5), .gt(comparator_1_gt), .eq(comparator_1_eq));  // open: lt
  Comparator #(.width(1)) comparator_2 (.a(a4), .b(b4), .gt(comparator_2_gt), .eq(comparator_2_eq));  // open: lt
  Comparator #(.width(1)) comparator_3 (.a(a3), .b(b3), .gt(comparator_3_gt), .eq(comparator_3_eq));  // open: lt
  Comparator #(.width(1)) comparator_4 (.a(a2), .b(b2), .gt(comparator_4_gt), .eq(comparator_4_eq));  // open: lt
  Comparator #(.width(1)) comparator_5 (.a(a1), .b(b1), .gt(comparator_5_gt), .eq(comparator_5_eq));  // open: lt
  Comparator #(.width(1)) comparator_6 (.a(a0), .b(b0), .gt(comparator_6_gt), .eq(comparator_6_eq));  // open: lt
  and and_1 (and_1_out, comparator_1_eq, comparator_2_gt);
  and and_2 (and_2_out, comparator_1_eq, comparator_2_eq, comparator_3_gt);
  and and_3 (and_3_out, comparator_1_eq, comparator_2_eq, comparator_3_eq, comparator_4_gt);
  and and_4 (and_4_out, comparator_1_eq, comparator_2_eq, comparator_3_eq, comparator_4_eq, comparator_5_gt);
  and and_5 (and_5_out, comparator_1_eq, comparator_2_eq, comparator_3_eq, comparator_4_eq, comparator_5_eq);
  and and_6 (and_6_out, comparator_6_gt, and_5_out);
  and and_7 (equal, and_5_out, comparator_6_eq);
  or or_1 (or_1_out, and_1_out, and_2_out, and_3_out, and_4_out, and_6_out);
  or or_2 (less_than, comparator_1_gt, or_1_out);
endmodule

// comparator
module Final_Score_Comparator_3term (
  input  p1a5,
  input  p2a5,
  input  p1a4,
  input  p2a4,
  input  p1a3,
  input  p2a3,
  input  p3a5,
  input  p1a2,
  input  p3a4,
  input  p2a2,
  input  p3a3,
  input  p1a1,
  input  p3a2,
  input  p2a1,
  input  p3a1,
  input  p1a0,
  input  p3a0,
  input  p2a0,
  output w1,
  output w0,
  output tie
);

  wire comparator_1_less_than, comparator_2_less_than, not_1_out, not_2_out, not_3_out,
       select_player_score_bits_1_a0, select_player_score_bits_1_a1, select_player_score_bits_1_a2,
       select_player_score_bits_1_a3, select_player_score_bits_1_a4, select_player_score_bits_1_a5;

  comparator comparator_1 (
    .a5(p1a5), .b5(p2a5), .a4(p1a4), .b4(p2a4), .a3(p1a3), .b3(p2a3), .a2(p1a2), .b2(p2a2), .a1(p1a1),
    .b1(p2a1), .a0(p1a0), .b0(p2a0), .less_than(comparator_1_less_than));  // open: equal
  not not_1 (not_1_out, comparator_1_less_than);
  select_player_score_bits select_player_score_bits_1 (
    .s1(comparator_1_less_than), .s0(not_1_out), .a0p1(p1a0), .a1p1(p1a1), .a2p1(p1a2), .a3p1(p1a3),
    .a4p1(p1a4), .a5p1(p1a5), .a0p2(p2a0), .a1p2(p2a1), .a2p2(p2a2), .a3p2(p2a3), .a4p2(p2a4), .a5p2(p2a5),
    .a0(select_player_score_bits_1_a0), .a1(select_player_score_bits_1_a1),
    .a2(select_player_score_bits_1_a2), .a3(select_player_score_bits_1_a3),
    .a4(select_player_score_bits_1_a4), .a5(select_player_score_bits_1_a5));  // open: a0p3, a1p3, a2p3, a3p3, a4p3, a5p3
  comparator comparator_2 (
    .a5(p3a5), .b5(select_player_score_bits_1_a5), .a4(p3a4), .b4(select_player_score_bits_1_a4), .a3(p3a3),
    .b3(select_player_score_bits_1_a3), .a2(p3a2), .b2(select_player_score_bits_1_a2), .a1(p3a1),
    .b1(select_player_score_bits_1_a1), .a0(p3a0), .b0(select_player_score_bits_1_a0),
    .less_than(comparator_2_less_than), .equal(tie));
  not not_2 (not_2_out, comparator_1_less_than);
  not not_3 (not_3_out, comparator_2_less_than);
  or or_1 (w1, comparator_1_less_than, not_3_out);
  or or_2 (w0, not_2_out, not_3_out);

  // Notes on the sheet:
  //   Final Score Comparator
  //   Draw
  //   WINNER CODE
  //   Winner MSB
  //   Winner LSB
endmodule

module Player_ID (
  input  Code_LSB,
  input  Code_MSB,
  output P1,
  output P2,
  output P3
);

  wire not_1_out, not_2_out;

  and and_1 (P3, Code_LSB, Code_MSB);
  not not_1 (not_1_out, Code_MSB);
  not not_2 (not_2_out, Code_LSB);
  and and_2 (P1, Code_LSB, not_1_out);
  and and_3 (P2, not_2_out, Code_MSB);

  // Notes on the sheet:
  //   Player ID
  //   Each player is assigned a 2-bit code using which 
  //   he gains access to the dart board and competes
  //   player-1
  //   player-2
  //   player-3
  //   CODE DETAILS
  //   00/01 ---> Player1
  //   10 ------>Player2
  //   11------>Player3
endmodule

module Main_DIGITAL_DART_GAME (
  input  READY,
  input  s1,
  input  s0,
  output w0,
  output w1,
  output DRAW
);

  wire achievement_unlocked_1_congrats, and_1_out, button_1_out, circle_points_1_s0, circle_points_1_s1,
       circle_points_1_s2, demux_a0p1, demux_a0p2, demux_a0p3, demux_a1p1, demux_a1p2, demux_a1p3,
       demux_a2p1, demux_a2p3, demux_a3p1, demux_a3p2, demux_a3p3, demux_a4p1, demux_a4p2, demux_a4p3,
       demux_a5p1, demux_a5p2, demux_a5p3, demux_a6p2, mux_a0, mux_a1, mux_a2, mux_a3, mux_a4, mux_a5,
       n5_bit_bcd_adder_1_o0, n5_bit_bcd_adder_1_o1, n5_bit_bcd_adder_1_o2, n5_bit_bcd_adder_1_o3,
       n5_bit_bcd_adder_1_o4, n5_bit_bcd_adder_1_o5, n7_segment_driver_1_a_2, n7_segment_driver_1_b_2,
       n7_segment_driver_1_c_2, n7_segment_driver_1_d_2, n7_segment_driver_1_e, n7_segment_driver_1_f,
       n7_segment_driver_1_g, n7_segment_driver_2_a_2, n7_segment_driver_2_b_2, n7_segment_driver_2_c_2,
       n7_segment_driver_2_d_2, n7_segment_driver_2_e, n7_segment_driver_2_f, n7_segment_driver_2_g,
       not_1_out, p1_register_o0, p1_register_o1, p1_register_o2, p1_register_o3, p1_register_o4,
       p1_register_o5, p2_register_o0, p2_register_o1, p2_register_o2, p2_register_o3, p2_register_o4,
       p2_register_o5, p3_register_o0, p3_register_o1, p3_register_o2, p3_register_o3, p3_register_o4,
       p3_register_o5, player_id_1_p1, player_id_1_p2, player_id_1_p3, player_id_2_p1, player_id_2_p2,
       player_id_2_p3, player_id_3_p1, player_id_3_p2, player_id_3_p3, prbs_flux_1_l0_2, prbs_flux_1_l1,
       prbs_flux_1_l2_2, prbs_flux_1_l3, prbs_flux_1_l4, release_toggle_1_p1, release_toggle_1_p2,
       release_toggle_1_p3, throw_counter_1_l0, throw_counter_1_l1, throw_counter_1_l2, throw_counter_1_l3,
       throw_counter_1_l4, who_hits_the_bullseye_1_good_aim, who_hits_the_bullseye_2_good_aim,
       who_hits_the_bullseye_3_good_aim, winner_identity_1_p1, winner_identity_1_p2, winner_identity_1_p3;

  Release_Toggle release_toggle_1 (
    .\release (button_1_out), .s1(s1), .s0(s0), .p1(release_toggle_1_p1), .p3(release_toggle_1_p3),
    .p2(release_toggle_1_p2));
  Button button_1 (.out(button_1_out));
  Player_ID player_id_1 (.Code_LSB(s0), .Code_MSB(s1), .P1(player_id_1_p1), .P2(player_id_1_p2), .P3(player_id_1_p3));
  LED led_1 (.in(player_id_1_p1));
  LED led_2 (.in(player_id_1_p2));
  LED led_3 (.in(player_id_1_p3));
  Register p1_register (
    .a5(demux_a5p1), .a4(demux_a4p1), .a3(demux_a3p1), .a2(demux_a2p1), .a1(demux_a1p1), .a0(demux_a0p1),
    .enable_by_clock(release_toggle_1_p1), .o5(p1_register_o5), .o4(p1_register_o4), .o3(p1_register_o3),
    .o2(p1_register_o2), .o1(p1_register_o1), .o0(p1_register_o0));  // open: clear
  Register p2_register (
    .a5(demux_a6p2), .a4(demux_a5p2), .a3(demux_a4p2), .a2(demux_a3p2), .a1(demux_a1p2), .a0(demux_a0p2),
    .enable_by_clock(release_toggle_1_p2), .o5(p2_register_o5), .o4(p2_register_o4), .o3(p2_register_o3),
    .o2(p2_register_o2), .o1(p2_register_o1), .o0(p2_register_o0));  // open: clear
  Register p3_register (
    .a5(demux_a5p3), .a4(demux_a4p3), .a3(demux_a3p3), .a2(demux_a2p3), .a1(demux_a1p3), .a0(demux_a0p3),
    .enable_by_clock(release_toggle_1_p3), .o5(p3_register_o5), .o4(p3_register_o4), .o3(p3_register_o3),
    .o2(p3_register_o2), .o1(p3_register_o1), .o0(p3_register_o0));  // open: clear
  Final_Score_Comparator_3term final_score_comparator_3term_1 (
    .p1a5(p1_register_o5), .p2a5(p2_register_o5), .p1a4(p1_register_o4), .p2a4(p2_register_o4),
    .p1a3(p1_register_o3), .p2a3(p2_register_o3), .p3a5(p3_register_o5), .p1a2(p1_register_o2),
    .p3a4(p3_register_o4), .p2a2(p2_register_o2), .p3a3(p3_register_o3), .p1a1(p1_register_o1),
    .p3a2(p3_register_o2), .p2a1(p2_register_o0), .p3a1(p3_register_o1), .p1a0(p1_register_o0),
    .p3a0(p3_register_o0), .p2a0(p2_register_o0), .w1(w0), .w0(w1), .tie(DRAW));
  select_player_score_bits mux (
    .s1(s1), .s0(s0), .a0p1(p1_register_o0), .a1p1(p1_register_o1), .a2p1(p1_register_o2),
    .a3p1(p1_register_o3), .a4p1(p1_register_o4), .a5p1(p1_register_o5), .a0p2(p2_register_o0),
    .a1p2(p2_register_o1), .a2p2(p2_register_o2), .a3p2(p2_register_o3), .a4p2(p2_register_o4),
    .a5p2(p2_register_o5), .a0p3(p3_register_o0), .a1p3(p3_register_o1), .a2p3(p3_register_o2),
    .a3p3(p3_register_o3), .a4p3(p3_register_o4), .a5p3(p3_register_o5), .a0(mux_a0), .a1(mux_a1),
    .a2(mux_a2), .a3(mux_a3), .a4(mux_a4), .a5(mux_a5));
  LED led_4 ();  // open: in
  Circle_Points circle_points_1 (
    .L0(prbs_flux_1_l0_2), .L1(prbs_flux_1_l1), .L2(prbs_flux_1_l2_2), .L3(prbs_flux_1_l4),
    .L4(prbs_flux_1_l4), .S0(circle_points_1_s0), .S1(circle_points_1_s1), .S2(circle_points_1_s2));
  _5_bit_bcd_adder u_5_bit_bcd_adder_1 (
    .b4(1'b0), .b3(1'b0), .b2(circle_points_1_s2), .b1(circle_points_1_s1), .b0(circle_points_1_s0),
    .a4(mux_a4), .a3(mux_a3), .a2(mux_a2), .a1(mux_a1), .a0(mux_a0), .o0(n5_bit_bcd_adder_1_o0),
    .o1(n5_bit_bcd_adder_1_o1), .o2(n5_bit_bcd_adder_1_o2), .o3(n5_bit_bcd_adder_1_o3),
    .o4(n5_bit_bcd_adder_1_o4), .o5(n5_bit_bcd_adder_1_o5));
  LED led_5 ();  // open: in
  LED led_6 ();  // open: in
  winner_identity winner_identity_1 (
    .s1(w0), .s0(w1), .p3(winner_identity_1_p3), .p2(winner_identity_1_p2), .p1(winner_identity_1_p1));
  LED led_7 ();  // open: in
  demux_6bit_for_player_scores demux (
    .s0(s0), .s1(s1), .a0(n5_bit_bcd_adder_1_o0), .a1(n5_bit_bcd_adder_1_o1), .a2(n5_bit_bcd_adder_1_o2),
    .a3(n5_bit_bcd_adder_1_o3), .a4(n5_bit_bcd_adder_1_o4), .a5(n5_bit_bcd_adder_1_o5), .a0p1(demux_a0p1),
    .a1p1(demux_a1p1), .a2p1(demux_a2p1), .a3p1(demux_a3p1), .a4p1(demux_a4p1), .a5p1(demux_a5p1),
    .a0p2(demux_a0p2), .a1p2(demux_a1p2), .a3p2(demux_a3p2), .a4p2(demux_a4p2), .a5p2(demux_a5p2),
    .a6p2(demux_a6p2), .a0p3(demux_a0p3), .a1p3(demux_a1p3), .a2p3(demux_a2p3), .a3p3(demux_a3p3),
    .a4p3(demux_a4p3), .a5p3(demux_a5p3));
  PRBS_FLUX prbs_flux_1 (
    .L0(throw_counter_1_l0), .RELEASE(button_1_out), .L2(throw_counter_1_l2), .READY(READY),
    .L4(prbs_flux_1_l4), .L3(prbs_flux_1_l3), .L2_2(prbs_flux_1_l2_2), .L1(prbs_flux_1_l1),
    .L0_2(prbs_flux_1_l0_2));
  LED led_8 (.in(prbs_flux_1_l4));
  LED led_9 (.in(prbs_flux_1_l4));
  LED led_10 (.in(prbs_flux_1_l4));
  LED led_11 (.in(prbs_flux_1_l4));
  Player_ID player_id_2 (.Code_LSB(s0), .Code_MSB(s1), .P1(player_id_2_p1), .P2(player_id_2_p2), .P3(player_id_2_p3));
  LED P1 (.in(player_id_2_p1));
  LED P2 (.in(player_id_2_p2));
  LED P3 (.in(player_id_2_p3));
  LED led_12 (.in(prbs_flux_1_l4));
  LED led_13 (.in(prbs_flux_1_l3));
  LED led_14 (.in(prbs_flux_1_l2_2));
  LED led_15 (.in(prbs_flux_1_l2_2));
  LED led_16 (.in(prbs_flux_1_l3));
  LED led_17 (.in(prbs_flux_1_l2_2));
  LED led_18 (.in(prbs_flux_1_l3));
  LED led_19 (.in(prbs_flux_1_l4));
  _7_Segment_Display u_7_segment_display_1 (
    .g(n7_segment_driver_1_g), .f(n7_segment_driver_1_f), .a(n7_segment_driver_1_a_2),
    .b(n7_segment_driver_1_b_2), .e(n7_segment_driver_1_e), .d(n7_segment_driver_1_d_2),
    .c(n7_segment_driver_1_c_2));  // open: dp
  LED led_20 (.in(prbs_flux_1_l3));
  LED led_21 (.in(prbs_flux_1_l1));
  LED led_22 (.in(prbs_flux_1_l1));
  LED led_23 (.in(prbs_flux_1_l0_2));
  LED led_24 (.in(prbs_flux_1_l1));
  LED led_25 (.in(prbs_flux_1_l3));
  _7_segment_driver u_7_segment_driver_1 (
    .A(1'b0), .B(1'b0), .C(mux_a5), .D(mux_a4), .a_2(n7_segment_driver_1_a_2), .b_2(n7_segment_driver_1_b_2),
    .c_2(n7_segment_driver_1_c_2), .d_2(n7_segment_driver_1_d_2), .e(n7_segment_driver_1_e),
    .f(n7_segment_driver_1_f), .g(n7_segment_driver_1_g));
  LED led_26 (.in(prbs_flux_1_l4));
  LED led_27 (.in(prbs_flux_1_l3));
  LED led_28 (.in(prbs_flux_1_l3));
  LED led_29 (.in(prbs_flux_1_l2_2));
  LED led_30 (.in(prbs_flux_1_l1));
  LED led_31 (.in(prbs_flux_1_l1));
  LED led_32 (.in(prbs_flux_1_l1));
  LED led_33 (.in(prbs_flux_1_l1));
  LED led_34 (.in(prbs_flux_1_l1));
  LED led_35 (.in(prbs_flux_1_l2_2));
  LED led_36 (.in(prbs_flux_1_l3));
  LED led_37 (.in(prbs_flux_1_l3));
  LED led_38 (.in(prbs_flux_1_l4));
  _7_segment_driver u_7_segment_driver_2 (
    .A(mux_a3), .B(mux_a2), .C(mux_a1), .D(mux_a0), .a_2(n7_segment_driver_2_a_2),
    .b_2(n7_segment_driver_2_b_2), .c_2(n7_segment_driver_2_c_2), .d_2(n7_segment_driver_2_d_2),
    .e(n7_segment_driver_2_e), .f(n7_segment_driver_2_f), .g(n7_segment_driver_2_g));
  _7_Segment_Display u_7_segment_display_2 (
    .g(n7_segment_driver_2_g), .f(n7_segment_driver_2_f), .a(n7_segment_driver_2_a_2),
    .b(n7_segment_driver_2_b_2), .e(n7_segment_driver_2_e), .d(n7_segment_driver_2_d_2),
    .c(n7_segment_driver_2_c_2));  // open: dp
  LED led_39 (.in(prbs_flux_1_l4));
  LED led_40 (.in(prbs_flux_1_l3));
  LED led_41 (.in(prbs_flux_1_l2_2));
  LED led_42 (.in(prbs_flux_1_l3));
  LED led_43 (.in(prbs_flux_1_l2_2));
  LED led_44 (.in(prbs_flux_1_l2_2));
  LED led_45 (.in(prbs_flux_1_l3));
  LED led_46 (.in(prbs_flux_1_l4));
  LED led_47 (.in(prbs_flux_1_l4));
  LED led_48 (.in(prbs_flux_1_l4));
  LED led_49 (.in(prbs_flux_1_l4));
  LED led_50 (.in(prbs_flux_1_l4));
  LED led_51 (.in(winner_identity_1_p1));
  not not_1 (not_1_out, button_1_out);
  and and_1 (and_1_out, prbs_flux_1_l0_2, not_1_out);
  LED led_52 (.in(achievement_unlocked_1_congrats));
  LED led_53 (.in(achievement_unlocked_1_congrats));
  LED led_54 (.in(achievement_unlocked_1_congrats));
  LED led_55 (.in(achievement_unlocked_1_congrats));
  LED led_56 (.in(achievement_unlocked_1_congrats));
  LED led_57 (.in(achievement_unlocked_1_congrats));
  LED led_58 (.in(winner_identity_1_p1));
  who_hits_the_bullseye who_hits_the_bullseye_1 (
    .player_code(player_id_3_p1), .Throw_Button(and_1_out), .GOOD_AIM(who_hits_the_bullseye_1_good_aim));
  LED led_59 (.in(winner_identity_1_p1));
  LED led_60 (.in(winner_identity_1_p1));
  LED led_61 (.in(winner_identity_1_p1));
  LED led_62 (.in(winner_identity_1_p1));
  LED led_63 (.in(winner_identity_1_p1));
  LED led_64 (.in(winner_identity_1_p1));
  LED led_65 (.in(winner_identity_1_p2));
  LED led_66 (.in(who_hits_the_bullseye_1_good_aim));
  LED led_67 (.in(who_hits_the_bullseye_1_good_aim));
  LED led_68 (.in(winner_identity_1_p2));
  LED led_69 (.in(who_hits_the_bullseye_1_good_aim));
  LED led_70 (.in(who_hits_the_bullseye_1_good_aim));
  LED led_71 (.in(winner_identity_1_p2));
  LED led_72 (.in(who_hits_the_bullseye_1_good_aim));
  LED led_73 (.in(who_hits_the_bullseye_1_good_aim));
  LED led_74 (.in(who_hits_the_bullseye_1_good_aim));
  LED led_75 (.in(who_hits_the_bullseye_1_good_aim));
  LED led_76 (.in(who_hits_the_bullseye_1_good_aim));
  Throw_Counter throw_counter_1 (
    .Throw(button_1_out), .L4(throw_counter_1_l4), .L3(throw_counter_1_l3), .L2(throw_counter_1_l2),
    .L1(throw_counter_1_l1), .L0(throw_counter_1_l0));
  Achievement_Unlocked achievement_unlocked_1 (.Bullseye(and_1_out), .Congrats(achievement_unlocked_1_congrats));
  LED led_77 (.in(achievement_unlocked_1_congrats));
  LED led_78 (.in(achievement_unlocked_1_congrats));
  LED led_79 (.in(achievement_unlocked_1_congrats));
  LED led_80 (.in(achievement_unlocked_1_congrats));
  LED led_81 (.in(achievement_unlocked_1_congrats));
  LED led_82 (.in(achievement_unlocked_1_congrats));
  LED led_83 (.in(achievement_unlocked_1_congrats));
  LED led_84 (.in(achievement_unlocked_1_congrats));
  LED led_85 (.in(achievement_unlocked_1_congrats));
  LED led_86 (.in(achievement_unlocked_1_congrats));
  who_hits_the_bullseye who_hits_the_bullseye_2 (
    .player_code(player_id_3_p2), .Throw_Button(and_1_out), .GOOD_AIM(who_hits_the_bullseye_2_good_aim));
  LED led_87 (.in(winner_identity_1_p2));
  LED led_88 (.in(winner_identity_1_p2));
  LED led_89 (.in(winner_identity_1_p2));
  LED led_90 (.in(winner_identity_1_p2));
  LED led_91 (.in(winner_identity_1_p2));
  LED led_92 (.in(winner_identity_1_p2));
  LED led_93 (.in(winner_identity_1_p2));
  LED led_94 (.in(winner_identity_1_p2));
  LED led_95 (.in(who_hits_the_bullseye_2_good_aim));
  LED led_96 (.in(who_hits_the_bullseye_2_good_aim));
  LED led_97 (.in(who_hits_the_bullseye_2_good_aim));
  LED led_98 (.in(winner_identity_1_p3));
  LED led_99 (.in(who_hits_the_bullseye_2_good_aim));
  LED led_100 (.in(throw_counter_1_l0));
  LED led_101 (.in(throw_counter_1_l0));
  LED led_102 (.in(throw_counter_1_l0));
  LED led_103 (.in(throw_counter_1_l0));
  LED led_104 (.in(throw_counter_1_l1));
  LED led_105 (.in(throw_counter_1_l1));
  LED led_106 (.in(throw_counter_1_l1));
  LED led_107 (.in(throw_counter_1_l1));
  LED led_108 (.in(throw_counter_1_l2));
  LED led_109 (.in(throw_counter_1_l2));
  LED led_110 (.in(throw_counter_1_l2));
  LED led_111 (.in(throw_counter_1_l2));
  LED led_112 (.in(throw_counter_1_l3));
  LED led_113 (.in(throw_counter_1_l3));
  LED led_114 (.in(throw_counter_1_l3));
  LED led_115 (.in(throw_counter_1_l3));
  LED led_116 (.in(throw_counter_1_l4));
  LED led_117 (.in(throw_counter_1_l4));
  LED led_118 (.in(throw_counter_1_l4));
  LED led_119 (.in(throw_counter_1_l4));
  who_hits_the_bullseye who_hits_the_bullseye_3 (
    .player_code(player_id_3_p3), .Throw_Button(and_1_out), .GOOD_AIM(who_hits_the_bullseye_3_good_aim));
  LED led_120 (.in(winner_identity_1_p3));
  LED led_121 (.in(winner_identity_1_p3));
  LED led_122 (.in(winner_identity_1_p3));
  LED led_123 (.in(winner_identity_1_p3));
  LED led_124 (.in(winner_identity_1_p3));
  LED led_125 (.in(winner_identity_1_p3));
  LED led_126 (.in(winner_identity_1_p3));
  LED led_127 (.in(winner_identity_1_p3));
  LED led_128 (.in(winner_identity_1_p3));
  LED led_129 (.in(winner_identity_1_p3));
  LED led_130 (.in(throw_counter_1_l0));
  LED led_131 (.in(throw_counter_1_l1));
  LED led_132 (.in(throw_counter_1_l2));
  LED led_133 (.in(throw_counter_1_l3));
  LED led_134 (.in(throw_counter_1_l4));
  Player_ID player_id_3 (.Code_LSB(s0), .Code_MSB(s1), .P1(player_id_3_p1), .P2(player_id_3_p2), .P3(player_id_3_p3));
  LED led_135 (.in(who_hits_the_bullseye_3_good_aim));
  LED led_136 (.in(who_hits_the_bullseye_3_good_aim));
  LED led_137 (.in(who_hits_the_bullseye_3_good_aim));

  // Notes on the sheet:
  //      ALL THE BEST
  //   Release toggle
  //   RULES :
  //   1) Each player gets 5 throws
  //   2)To throw the dart, first aim by 
  //   pressing the throw button and
  //     and then throw by releasing..
  //    3)Only one player at a time
  //   THROW
  //   select player
  //   P1
  //   P2
  //      P3
  //   PLAYER
  //     P1
  //   P2
  //   P3
  //   2-BIT PLAYER CODE :
  //     PLAYER1----> 00/01
  //   PLAYER2----> 10
  //   PLAYER3---->11
  //   Quiver is full
  //   POINTS CALC
  //   - - - - - - >
  //   WINNING CODE
  //   Quiver will empty soon
  //   PRBS FLUX
  //   Player Identity
  //   5 !!!
  //   4 Points
  //   " AIM TRUE, SCORE HIGH, AND NEVER MISS YOUR MARK ! "
  //   AIM AND FAME
  //   3 Points
  //   TARGET TALLY
  //   2 Points
  //   1 Points
  //   THROWS LEFT
  //   BULLSEYE
  //   Achivement Unlocked
  //   Your Quiver
  //   ----
  //    5
  //   4
  //   ----
  //   3
  //   ----
  //   ----
  //   2
  //   1
  //   ----
  //   CONTROLS :
  //   OBJECTIVE :
  //   THE DARTBOARD.
  //   SCORE AT THE END.
  //   SETUP :
  //   NO CIRCLE --->0 POINTS
  //   END OF GAME :
  //   ALL FOR THE BULLSEYE ?
  //   LET THE BEST PLAYER WIN.
  //   PRESS THROW BUTTON TO THROW 
  //   THE DART WHEN THE LED SEQUENCE
  //   REACHES YOUR TARGET.
  //   PLAYER SELECTION SWITCH :
  //   USE THIS SWITCH BETWEEN PLAYERS
  //   IN MULTIPLAYER MODE.
  //   THE OBJECTIVE OF THE GAME IS TO
  //   SCORE AS MANY POINTS AS POSSIBLE 
  //   BY TIMING YOUR THROW WHEN LED SEQUENCE
  //   ALIGNS WITH THE HIGH-SCORING AREAS OF
  //   GAME CAN BE PLAYED BY MULTIPLE PLAYERS
  //   AND WINNER IS PLAYER WITH THE HIGHEST
  //   THE DARTBOARD CONSISTS OF 5
  //   CONCENTRIC CIRCLES EACH
  //   REPRESENTED BY AN ARRAY OF LEDS
  //   THE POINT VALUES FROM OUTER TO INNER
  //   OUTER CIRCLE ---> 1 POINTS
  //   PENULTIMATE CIRCLE --->2 POINTS
  //   MIDDLE CIRCLE ---> 3 POINTS
  //   SECOND INNER CIRCLE ---> 4 POINTS
  //   INNER CIRCLE( BULLSEYE ) --->5 POINTS
  //   AFTER EVERY PLAYER TAKES 5 THROWS
  //   THE WINNER IS DISPLAYED ON THE SCREEN
  //   IN CASE OF TIE, THERE IS SUDDEN DEATH ROUND 
  //   WITH ONE EXTRA THROW TO EACH PLAYER
  //   NOW THAT YOU KNOW THE RULES,
  //   IT'S TIME TO TEST YOUR TIMING, PRECISION
  //   AND STRATEGY! WILL YOU GO FOR
  //   THE SAFE OUTER CIRCLES OR RISK IT
  //   STEP UP, HIT THE THROW BUTTON AND
  //   HOW TO PLAY :
  //   MAY THE BULESEYE BE EVER IN YOUR FAVOR!
  //   GAME ON!
endmodule

module Achievement_Unlocked (
  input  Bullseye,
  output Congrats
);

  wire clock_1_out, not_1_out;

  Clock clock_1 (.out(clock_1_out));
  not not_1 (not_1_out, Bullseye);
  T_Flip_Flop t_ff_1 (.clk(clock_1_out), .T(Bullseye), .Q(Congrats), .reset(not_1_out));  // open: Qn, preset, en

  // Notes on the sheet:
  //   Achievement Unlocked
  //   Bulleye is always a matter of celebration and 
  //   we implement that by a toggling structure of 5 
  //   implemented by LEDS
endmodule

module winner_identity (
  input  s1,
  input  s0,
  output p3,
  output p2,
  output p1
);

  wire not_1_out;

  and and_1 (p3, s0, s1);
  and and_2 (p2, s1, not_1_out);
  not not_1 (not_1_out, s0);
  not not_2 (p1, s1);

  // Notes on the sheet:
  //   PLAYER CODE
  //   CODE MSB
  //   CODE LSB
  //   Winner Identity Code
  //   TIE BREAKER
  //   WINNER CODE
  //   CODE MSB
  //   CODE LSB
endmodule

module who_hits_the_bullseye (
  input  player_code,
  input  Throw_Button,
  output GOOD_AIM
);

  wire and_1_out, clk_out, not_1_out;

  and and_1 (and_1_out, player_code, Throw_Button);
  not not_1 (not_1_out, and_1_out);
  Clock clk (.out(clk_out));
  T_Flip_Flop t_ff_1 (.clk(clk_out), .T(and_1_out), .Q(GOOD_AIM), .reset(not_1_out));  // open: Qn, preset, en

  // Notes on the sheet:
  //   RECOGNITION OF ACHIEVEMENT
  //   TOGGLING EFFECT OF LED WHEN PLAYER HITS THE BULLSEYE AND SCORES 5 POINTS
  //   THIS GIVES DUE RECOGNITION TO THE PLAYERS ACHIEVEMENT
  //   clear
endmodule

module Throw_Counter (
  input  Throw,
  output L4,
  output L3,
  output L2,
  output L1,
  output L0
);

  wire and_2_out, and_3_out, j_k_ff_1_q, j_k_ff_1_qn, j_k_ff_2_q, j_k_ff_2_qn, j_k_ff_3_q, not_1_out,
       not_2_out, not_3_out;

  J_K_Flip_Flop j_k_ff_1 (
    .J(1'b1), .clk(Throw), .K(1'b1), .Q(j_k_ff_1_q), .Qn(j_k_ff_1_qn), .reset(L4));  // open: preset, en
  not not_1 (not_1_out, and_2_out);
  and and_1 (L4, j_k_ff_1_q, not_1_out, L3);
  J_K_Flip_Flop j_k_ff_2 (
    .J(1'b1), .clk(j_k_ff_1_qn), .K(1'b1), .Q(j_k_ff_2_q), .Qn(j_k_ff_2_qn), .reset(L4));  // open: preset, en
  not not_2 (not_2_out, j_k_ff_3_q);
  and and_2 (and_2_out, j_k_ff_2_q, not_2_out);
  and and_3 (and_3_out, and_2_out, j_k_ff_1_q);
  or or_1 (L2, L3, and_3_out);
  or or_2 (L0, j_k_ff_1_q, and_2_out, L3);
  or or_3 (L1, and_2_out, L3);
  J_K_Flip_Flop j_k_ff_3 (.J(1'b1), .clk(j_k_ff_2_qn), .K(1'b1), .Q(j_k_ff_3_q), .reset(L4));  // open: Qn, preset, en
  not not_3 (not_3_out, j_k_ff_2_q);
  and and_4 (L3, not_3_out, j_k_ff_3_q);

  // Notes on the sheet:
  //   Constant High
  //   5 Throws
  //   TC_LSB
  //   4 Throw
  //   TC_1
  //   3 Throws
  //   2 Throws
  //   THROW COUNTER / DARTS IN QUIVER
  //   TC_MSB
  //   1 Throws
  //   THE BINARY THROW COUNT BITS ARE 
  //   MODIFIED TO CORRESPONDING DECIMAL NOS.
  //   SIGNIFYING THE DARTS LEFT IN THE QUIVER
  //   FROM 1 TO 5
  //   OF THE PLAYER
endmodule

module Release_Toggle (
  input  \release ,
  input  s1,
  input  s0,
  output p1,
  output p2,
  output p3
);

  wire and_1_out, and_2_out, and_3_out, j_k_ff_1_q, j_k_ff_2_q, j_k_ff_3_q, not_1_out, not_2_out, xor_1_out,
       xor_2_out, xor_3_out;

  not not_1 (not_1_out, s1);
  not not_2 (not_2_out, s0);
  and and_1 (and_1_out, not_1_out, s0);
  and and_2 (and_2_out, s1, not_2_out);
  and and_3 (and_3_out, s1, s0);
  xor xor_1 (xor_1_out, j_k_ff_1_q, \release );
  J_K_Flip_Flop j_k_ff_1 (
    .J(and_1_out), .clk(xor_1_out), .K(and_1_out), .Q(j_k_ff_1_q), .Qn(p1));  // open: preset, en, reset
  xor xor_2 (xor_2_out, j_k_ff_2_q, \release );
  J_K_Flip_Flop j_k_ff_2 (
    .J(and_2_out), .clk(xor_2_out), .K(and_2_out), .Q(j_k_ff_2_q), .Qn(p2));  // open: preset, en, reset
  xor xor_3 (xor_3_out, j_k_ff_3_q, \release );
  J_K_Flip_Flop j_k_ff_3 (
    .J(and_3_out), .clk(xor_3_out), .K(and_3_out), .Q(j_k_ff_3_q), .Qn(p3));  // open: preset, en, reset

  // Notes on the sheet:
  //   Release Toggle - 
  //   Use as enable for player registers
endmodule
